# Fritzing sketch simone (saved by Fritzing 0.9.3b)
breadboards: 1

parts:
  J2 = STM32 Nucleo boards
  R2 = Resistor [tolerance=±5% resistance=150 package="0603 [SMD]"]
  LED2 = RGB LED (com. cathode, rbg) [package="5 mm [THT]"]
  R5 = Resistor [tolerance=±5% resistance=91 package=THT]
  R8 = Resistor [tolerance=±5% resistance=91 package=THT]
  Keypad4x1 = Keypad Membran 4x4

nets:
  N1: J2.A0, Keypad4x1.Pin1
  N2: J2.A1, Keypad4x1.Pin2
  N3: J2.A2, Keypad4x1.Pin3
  N4: J2.A3, Keypad4x1.Pin4
  N5: J2.D10_PWM/SS, R2.Pin_0
  N6: J2.A4/SDA, R5.Pin_0
  N7: J2.A5/SCL, R8.Pin_0
  N8: J2.D0/RX, Keypad4x1.Pin8
  N9: J2.D1/TX, Keypad4x1.Pin7
  N10: J2.D2, Keypad4x1.Pin6
  N11: J2.D3_PWM, Keypad4x1.Pin5
  N12: J2.GND, LED2.common_cathode
  N13: R2.Pin_1, LED2.red_anode
  N14: LED2.blue_anode, R8.Pin_1
  N15: LED2.green_anode, R5.Pin_1

custom parts:
  Keypad Membran 4x4: Membrane Keypad 4x4 Matrix
