# Fritzing sketch simone_keyboard (saved by Fritzing 0.9.3b)
breadboards: 1

parts:
  J2 = STM32 Nucleo boards
  Keypad4x1 = Keypad Membran 4x4

nets:
  N1: J2.A0, Keypad4x1.Pin1
  N2: J2.A1, Keypad4x1.Pin2
  N3: J2.A2, Keypad4x1.Pin3
  N4: J2.A3, Keypad4x1.Pin4
  N5: J2.D0/RX, Keypad4x1.Pin8
  N6: J2.D1/TX, Keypad4x1.Pin7
  N7: J2.D2, Keypad4x1.Pin6
  N8: J2.D3_PWM, Keypad4x1.Pin5

custom parts:
  Keypad Membran 4x4: Membrane Keypad 4x4 Matrix
