# Fritzing sketch simone_rgb (saved by Fritzing 0.9.3b)
breadboards: 1

parts:
  J2 = STM32 Nucleo boards
  R5 = Resistor [tolerance=±5% resistance=91 package=THT]
  R8 = Resistor [tolerance=±5% resistance=91 package=THT]
  LED2 = RGB LED (com. cathode, rbg) [package="5 mm [THT]"]
  R2 = Resistor [tolerance=±5% resistance=150 package="0603 [SMD]"]

nets:
  N1: J2.D10_PWM/SS, R2.Pin_0
  N2: J2.A4/SDA, R5.Pin_0
  N3: J2.A5/SCL, R8.Pin_0
  N4: J2.GND, LED2.common_cathode
  N5: R5.Pin_1, LED2.green_anode
  N6: R8.Pin_1, LED2.blue_anode
  N7: LED2.red_anode, R2.Pin_1
